// Logisim project modelo_banco_registradores.circ as structural Verilog: 4 circuits, main circuit Bloco_Registradores
module Bloco_Registradores (
  input  [7:0] Data_in,
  input  Load,
  input  [7:0] Address_A_OUT,
  input  [1:0] Address_A,
  input  [1:0] Data_address,
  input  [7:0] Address_B_OUT,
  input  [1:0] Address_B,
  input  Clock
);

  wire and_1_out, and_2_out, and_3_out, decoder_1_out0, decoder_1_out1, decoder_1_out2;
  wire [7:0] R1_q, R2_q, R3_q;

  Decoder #(.select(2)) decoder_1 (
    .out0(decoder_1_out0), .out1(decoder_1_out1), .out2(decoder_1_out2), .sel(Data_address));  // open: out3, en
  Register R1 (.D(Data_in), .en(and_1_out), .clk(Clock), .Q(R1_q), .clr(1'b0));
  and and_1 (and_1_out, Load, decoder_1_out0);
  Register R2 (.D(Data_in), .en(and_2_out), .clk(Clock), .Q(R2_q), .clr(1'b0));
  and and_2 (and_2_out, Load, decoder_1_out1);
  Register R3 (.D(Data_in), .en(and_3_out), .clk(Clock), .Q(R3_q), .clr(1'b0));
  and and_3 (and_3_out, Load, decoder_1_out2);
  Multiplexer #(.select(2), .width(8)) multiplexer_1 (
    .in0({8{1'b0}}), .in1(R1_q), .in2(R2_q), .in3(R3_q), .out(Address_A_OUT), .sel(Address_A));
  Multiplexer #(.select(2), .width(8)) multiplexer_2 (
    .in0({8{1'b0}}), .in1(R1_q), .in2(R2_q), .in3(R3_q), .out(Address_B_OUT), .sel(Address_B));

  // Notes on the sheet:
  //   Data_in: initial=0x1
  //   R0
endmodule

module ULA (
  input  [7:0] Operando_A,
  input  [7:0] Resultado_ULA,
  input  [7:0] Operando_B
);

  Adder adder_1 (.a(Operando_A), .b(Operando_B), .out(Resultado_ULA));  // open: cin, cout
endmodule

module CPU_Principal (
  input  Mem_to_Reg
);

  wire [7:0] multiplexer_1_out, undriven, undriven_2, undriven_3;

  Multiplexer #(.width(8)) multiplexer_1 (.in0(undriven), .out(multiplexer_1_out), .sel(Mem_to_Reg));  // open: in1
  Bloco_Registradores bloco_registradores_1 (
    .Data_in(multiplexer_1_out), .Address_A_OUT(undriven_2), .Address_B_OUT(undriven_3));  // open: Load, Address_A, Data_address, Address_B, Clock
  ULA ula_1 (.Operando_A(undriven_2), .Resultado_ULA(undriven), .Operando_B(undriven_3));
endmodule

module Unidade_de_Controle (
  input  [1:0] Opcode,
  output Mem_to_Reg,
  output MemWrite,
  output Load
);

  wire decoder_1_out2;

  Decoder #(.select(2)) decoder_1 (
    .out0(Mem_to_Reg), .out1(MemWrite), .out2(decoder_1_out2), .sel(Opcode), .en(1'b1));  // open: out3
  or or_1 (Load, Mem_to_Reg, decoder_1_out2);
endmodule
